// Logisim project uebung02.circ as structural Verilog
module Volladdierer (
  input  E,
  input  A0,
  input  B0,
  output S0,
  output Carry_out
);

  wire and_1_out, and_2_out, xor_1_out;

  and and_1 (and_1_out, A0, B0);
  xor xor_1 (xor_1_out, A0, B0);
  and and_2 (and_2_out, xor_1_out, E);
  xor xor_2 (S0, E, xor_1_out);
  or or_1 (Carry_out, and_2_out, and_1_out);
endmodule

module Carry_select_adder (
  input  A0,
  input  A1,
  input  A2,
  input  A3,
  input  B0,
  input  B1,
  input  B2,
  input  B3,
  output a0_2,
  output a1_2,
  output a2_2,
  output a3_2,
  output c
);

  wire not_1_out, not_2_out, volladdierer_1_carry_out, volladdierer_2_carry_out, volladdierer_3_carry_out,
       volladdierer_3_s0, volladdierer_4_carry_out, volladdierer_4_s0, volladdierer_5_carry_out,
       volladdierer_5_s0, volladdierer_6_carry_out, volladdierer_6_s0;

  not not_1 (not_1_out, 1'b1);
  Volladdierer volladdierer_1 (.E(not_1_out), .A0(A0), .B0(B0), .S0(a0_2), .Carry_out(volladdierer_1_carry_out));
  Volladdierer volladdierer_2 (
    .E(volladdierer_1_carry_out), .A0(A1), .B0(B1), .S0(a1_2), .Carry_out(volladdierer_2_carry_out));
  Volladdierer volladdierer_3 (
    .E(not_2_out), .A0(A2), .B0(B2), .S0(volladdierer_3_s0), .Carry_out(volladdierer_3_carry_out));
  Volladdierer volladdierer_4 (
    .E(1'b1), .A0(A2), .B0(B2), .S0(volladdierer_4_s0), .Carry_out(volladdierer_4_carry_out));
  Volladdierer volladdierer_5 (
    .E(volladdierer_4_carry_out), .A0(A2), .B0(B3), .S0(volladdierer_5_s0),
    .Carry_out(volladdierer_5_carry_out));
  not not_2 (not_2_out, 1'b1);
  Volladdierer volladdierer_6 (
    .E(volladdierer_3_carry_out), .A0(A3), .B0(B3), .S0(volladdierer_6_s0),
    .Carry_out(volladdierer_6_carry_out));
  _6_auf_3_Mux u_6_auf_3_mux_1 (
    .e0(volladdierer_3_s0), .e1(volladdierer_6_s0), .e2(volladdierer_6_carry_out), .f0(volladdierer_4_s0),
    .f1(volladdierer_5_s0), .f2(volladdierer_5_carry_out), .C(volladdierer_2_carry_out), .out_8(a2_2),
    .out_9(a3_2), .out_10(c));
endmodule

module _6_auf_3_Mux (
  input  e0,
  input  e1,
  input  e2,
  input  f0,
  input  f1,
  input  f2,
  input  C,
  output out_8,
  output out_9,
  output out_10
);

  wire and_1_out, and_2_out, and_3_out, and_4_out, and_5_out, and_6_out, not_1_out;

  not not_1 (not_1_out, C);
  and and_1 (and_1_out, not_1_out, e0);
  and and_2 (and_2_out, not_1_out, e1);
  and and_3 (and_3_out, not_1_out, e2);
  and and_4 (and_4_out, C, f0);
  and and_5 (and_5_out, C, f1);
  and and_6 (and_6_out, C, f2);
  or or_1 (out_8, and_1_out, and_4_out);
  or or_2 (out_9, and_2_out, and_5_out);
  or or_3 (out_10, and_3_out, and_6_out);
endmodule
